# Fritzing sketch DIMMER MODULE (saved by Fritzing 0.9.4)
breadboards: 1

parts:
  Part1 = Arduino Nano (Rev3.0)
  Triac_Dimmer = IC, DIP package, 8 pins [chip_label=TRIAC]
  BULB1 = Incandescent light bulb small [package="bulb sm"]
  R1 = Photocell (LDR) [package=THT]
  R2 = Resistor [tolerance=±5% resistance=10k package=THT]

nets:
  N1: Part1.GND, Triac_Dimmer.pin4, R2.Pin_1
  N2: Part1.D3, Triac_Dimmer.pin2
  N3: Part1.5V, Triac_Dimmer.pin1, R1.pin_0
  N4: Part1.A6, R1.pin_1, R2.Pin_0
  N5: Triac_Dimmer.pin5, BULB1.2
  N6: Triac_Dimmer.pin6, BULB1.1
  GND: Triac_Dimmer.pin7
  120V: Triac_Dimmer.pin8
