# Fritzing sketch WarningLights (saved by Fritzing 0.9.4)
breadboards: 1

parts:
  Relay1 = RELAY [package=relay-t9a-2]
  R1 = Resistor [tolerance=±5% resistance=220 package=THT]
  BLUE_LED = smd LED [color="Red (633nm)" package="1206 [SMD]"]
  Relay2 = RELAY [package=relay-t9a-2]
  R2 = Resistor [tolerance=±5% resistance=220 package=THT]
  GREEN_LED = smd LED [color="Red (633nm)" package="1206 [SMD]"]
  Relay4 = RELAY [package=relay-t9a-2]
  Relay3 = RELAY [package=relay-t9a-2]
  R3 = Resistor [tolerance=±5% resistance=220 package=THT]
  R4 = Resistor [tolerance=±5% resistance=220 package=THT]
  RED_LED = smd LED [color="Red (633nm)" package="1206 [SMD]"]
  YELLOW_LED = smd LED [color="Red (633nm)" package="1206 [SMD]"]
  Part1 = Arduino Nano (Rev3.0) (ICSP)

nets:
  N1: Relay1.COIL1, Part1.D8
  GND: Relay1.COIL2, BLUE_LED.cathode, Relay2.COIL2, GREEN_LED.cathode, Relay4.COIL2, Relay3.COIL2, RED_LED.cathode, YELLOW_LED.cathode, Part1.GND
  5V: Relay1.MAIN, Relay2.MAIN, Relay4.MAIN, Relay3.MAIN
  N2: Relay1.NO, R1.Pin_0
  N3: R1.Pin_1, BLUE_LED.anode
  N4: Relay2.COIL1, Part1.D7
  N5: Relay2.NO, R2.Pin_0
  N6: R2.Pin_1, GREEN_LED.anode
  N7: Relay4.COIL1, Part1.D5
  N8: Relay4.NO, R3.Pin_0
  N9: Relay3.COIL1, Part1.D6
  N10: Relay3.NO, R4.Pin_0
  N11: R3.Pin_1, RED_LED.anode
  N12: R4.Pin_1, YELLOW_LED.anode
