# Fritzing sketch sensor module schematic (saved by Fritzing 0.9.4)
circuit board: 8.5cm x 6cm
breadboards: 1

parts:
  R1 = Resistor [tolerance=±1% resistance=10k package="1206 [SMD]"]
  R2 = PHOTOCELL [package=photocell]
  R3 = Resistor [tolerance=±1% resistance=10k package="1206 [SMD]"]
  R4 = Temperature Sensor (Thermistor) [thermistor_type=NTC package=THT]
  HC-SR04_Sensor_1 = HC-SR04 Ultrasonic Distance Sensor
  ZS-042_RTC1 = ZS-042 RTC Module
  HC-SR04_Sensor_2 = HC-SR04 Ultrasonic Distance Sensor
  Part1 = Arduino Nano (Rev3.0)

nets (from the schematic view):
  VCC: R1.Pin_0, R3.Pin_0, HC-SR04_Sensor_1.VCC, ZS-042_RTC1.VCC, HC-SR04_Sensor_2.VCC, Part1.5V
  N1: R1.Pin_1, R2.P$1, Part1.A0
  GND: R2.P$2, R4.pin_0, HC-SR04_Sensor_1.ECHO, ZS-042_RTC1.GND#0, HC-SR04_Sensor_2.ECHO, Part1.GND
  N2: R3.Pin_1, R4.pin_1, Part1.A1
  N3: HC-SR04_Sensor_1.TRIG, Part1.D3
  N4: HC-SR04_Sensor_1.GND, Part1.D4
  N5: ZS-042_RTC1.SDA, Part1.D11/MOSI
  N6: ZS-042_RTC1.SCL, Part1.D12/MISO
  N7: HC-SR04_Sensor_2.TRIG, Part1.D5
  N8: HC-SR04_Sensor_2.GND, Part1.D6
